# Fritzing sketch esquematico (saved by Fritzing 0.9.3b)
breadboards: 1

parts:
  Part1 = LC Studio SD Card Module
  Part2 = Arduino Mega 2560 (Rev3)
  R1 = Resistor [tolerance=±5% resistance=220 package="2010 [SMD]"]
  R7 = Resistor [tolerance=±5% resistance=220 package="2010 [SMD]"]  # not connected
  R8 = Resistor [tolerance=±5% resistance=220 package="2010 [SMD]"]
  R9 = Resistor [tolerance=±5% resistance=220 package="2010 [SMD]"]  # not connected
  R10 = Resistor [tolerance=±5% resistance=220 package="2010 [SMD]"]  # not connected
  R11 = Resistor [tolerance=±5% resistance=220 package="2010 [SMD]"]  # not connected
  ZS-042_RTC1 = ZS-042 RTC Module  # not connected

nets:
  5V: Part1.5V, Part2.5V
  N1: Part1.CS, R1.Pin_1, R8.Pin_0
  GND: Part1.GND, Part2.GND, R1.Pin_0
  N2: Part2.D4_PWM, R8.Pin_1

custom parts:
  LC Studio SD Card Module: The LC Studio SD card module serves as an interface to an SD card. The module works at 3.3 volts and 5 volts. The SPI (Serial Peripheral Interface) protocol is used for communicating with the module.
